# Fritzing sketch AND gate (saved by Fritzing 1.0.3b)
breadboards: 1

parts:
  VCC1 = Battery [internal_resistance=0.1Ω]
  S2 = Pushbutton [package="[THT]"]
  S3 = Pushbutton [package="[THT]"]
  R1 = Resistor [tolerance=±5% resistance=220 package="2512 [SMD]"]
  R2 = Resistor [tolerance=±5% resistance=220 package="2512 [SMD]"]
  Q1 = NPN-Transistor [package="TO92 [THT]"]
  Q2 = NPN-Transistor [package="TO92 [THT]"]
  LED1 = LED - 5mm [color="Red (633nm)" current=0.030A package="5 mm [THT]"]

nets:
  N1: VCC1.-, Q2.B, LED1.cathode, LED1.anode
  N2: VCC1.+, S2.Pin_1, S2.Pin_2, S2.Pin_3, S2.Pin_4, S3.Pin_1, S3.Pin_2, S3.Pin_3, S3.Pin_4, R1.Pin_0, R2.Pin_1, Q1.E
  N3: R1.Pin_1, Q1.C
  N4: R2.Pin_0, Q2.C
  N5: Q1.B, Q2.E
