# Fritzing sketch CMOS_NAND_Gate (saved by Fritzing 1.0.3b)
breadboards: 1

parts:
  VCC1 = Battery [internal_resistance=0.1Ω]
  S1 = Pushbutton [package="[THT]"]
  S2 = Pushbutton [package="[THT]"]
  Q1 = Basic FET P-Channel [package="DPak [SMD]"]
  Q2 = Basic FET P-Channel [package="DPak [SMD]"]
  Q3 = Basic FET N-Channel [package="TO220 [THT]"]
  Q4 = Basic FET N-Channel [package="TO220 [THT]"]
  R1 = Resistor [tolerance=±5% power=0.25W resistance=220 package=THT]
  LED1 = LED - 5mm [color="Red (633nm)" current=0.030A package="5 mm [THT]"]

nets:
  N1: VCC1.-, Q4.source
  N2: VCC1.+, S1.Pin_1, S1.Pin_2, S1.Pin_3, S1.Pin_4, S2.Pin_1, S2.Pin_2, S2.Pin_3, S2.Pin_4, Q1.Gate, Q1.drain, Q2.Gate, Q2.drain, Q3.drain, Q4.gate
  N3: Q1.source, Q2.source, Q3.gate, R1.Pin_1
  N4: Q3.source, Q4.drain
  N5: R1.Pin_0, LED1.anode
