# Fritzing sketch LED flasher (saved by Fritzing 1.0.3b)
breadboards: 1

parts:
  VCC1 = Battery [internal_resistance=0.1Ω]
  LED1 = LED - 5mm [color="Red (633nm)" current=0.030A package="5 mm [THT]"]
  R1 = Resistor [tolerance=±5% resistance=220 package="2512 [SMD]"]
  R2 = Resistor [tolerance=±5% resistance=220 package="2512 [SMD]"]
  LED2 = LED - 5mm [color="Red (633nm)" current=0.030A package="5 mm [THT]"]
  R3 = Resistor [tolerance=±5% resistance=220 package="2512 [SMD]"]
  R4 = Resistor [tolerance=±5% resistance=220 package="2512 [SMD]"]
  C1 = Electrolytic Capacitor [capacitance=1μF voltage=35V package="0405 [SMD, electrolytic]"]
  C2 = Electrolytic Capacitor [capacitance=1μF voltage=35V package="0405 [SMD, electrolytic]"]
  Q1 = NPN-Transistor [package="TO92 [THT]"]
  Q2 = NPN-Transistor [package="TO92 [THT]"]

nets:
  N1: VCC1.-, Q1.B, Q2.B
  N2: VCC1.+, LED1.anode, R1.Pin_1, R2.Pin_1, LED2.anode
  N3: LED1.cathode, R3.Pin_0, R3.Pin_1, C1.-
  N4: R1.Pin_0, C1.+, Q1.E, Q2.C
  N5: R2.Pin_0, C2.-
  N6: R4.Pin_0, R4.Pin_1, C2.+, Q1.C
