# Fritzing sketch NOR_Gate (saved by Fritzing 1.0.3b)
breadboards: 1

parts:
  VCC1 = Battery [internal_resistance=0.1Ω]
  S1 = Pushbutton [package="[THT]"]
  S2 = Pushbutton [package="[THT]"]
  R1 = Resistor [tolerance=±5% resistance=220 package="2512 [SMD]"]
  LED1 = LED - 5mm [color="Red (633nm)" current=0.030A package="5 mm [THT]"]
  R2 = Resistor [tolerance=±5% power=0.25W resistance=220 package=THT]
  R3 = Resistor [tolerance=±5% power=0.25W resistance=220 package=THT]

nets:
  N1: VCC1.-, LED1.anode, R2.Pin_1, R3.Pin_1
  N2: VCC1.+, S1.Pin_1, S1.Pin_2, S1.Pin_3, S1.Pin_4, S2.Pin_1, S2.Pin_2, S2.Pin_3, S2.Pin_4, R1.Pin_1, R2.Pin_0, R3.Pin_0
  N3: R1.Pin_0, LED1.cathode
