# Fritzing sketch NOT Gate (saved by Fritzing 1.0.3b)
breadboards: 1

parts:
  BAT1 = Battery Holders [package=lipo-1100mAh]
  S1 = Pushbutton [package="[THT]"]
  R1 = Resistor [tolerance=±5% power=0.25W resistance=220 package=THT]
  LED1 = LED - 5mm [color="Red (633nm)" current=0.030A package="5 mm [THT]"]
  Q1 = NPN-Transistor [package="TO92 [THT]"]
  R2 = Resistor [tolerance=±5% power=0.25W resistance=220 package=THT]
  LED2 = LED - 5mm [color="Red (633nm)" current=0.030A package="5 mm [THT]"]

nets:
  N1: BAT1.+, S1.Pin_1, S1.Pin_2, S1.Pin_3, S1.Pin_4, R1.Pin_0, R2.Pin_1, LED2.cathode
  N2: BAT1.-, Q1.E, LED2.anode
  N3: R1.Pin_1, LED1.cathode
  N4: LED1.anode, Q1.C
  N5: Q1.B, R2.Pin_0
