# Fritzing sketch Full_wave_rectifier (saved by Fritzing 1.0.3b)
breadboards: 1

parts:
  D1 = Rectifier Diode [part_number=1N4001 package="300 mil [THT]"]
  D2 = Rectifier Diode [part_number=1N4001 package="300 mil [THT]"]
  D3 = Rectifier Diode [part_number=1N4001 package="300 mil [THT]"]
  D4 = Rectifier Diode [part_number=1N4001 package="300 mil [THT]"]
  C1 = Tantalum Capacitor [capacitance=1μF voltage=35V package="100 mil [THT, tantalum]"]
  R1 = Resistor [tolerance=±5% power=0.25W resistance=220 package=THT]

nets:
  N1: D1.cathode, D4.anode
  N2: D1.anode, D3.anode
  N3: D2.cathode, D4.cathode, C1.-, R1.Pin_0
  N4: D2.anode, D3.cathode
