# Fritzing sketch Half_wave_rectifier (saved by Fritzing 1.0.3b)
breadboards: 1

parts:
  D1 = Rectifier Diode [part_number=1N4001 package="300 mil [THT]"]
  R1 = Resistor [tolerance=±5% power=0.25W resistance=220 package=THT]

nets:
  N1: D1.anode, R1.Pin_0
