# Fritzing sketch Audio_Amplifier (saved by Fritzing 1.0.3b)
breadboards: 1

parts:
  J1 = Piezo Speaker
  VCC1 = Battery block 9V [internal_resistance=0.1Ω]
  R1 = Resistor [tolerance=±5% power=0.25W resistance=220 package=THT]
  R2 = Resistor [tolerance=±5% power=0.25W resistance=220 package=THT]
  Q1 = NPN-Transistor [package="TO92 [THT]"]
  R3 = Resistor [tolerance=±5% power=0.25W resistance=220 package=THT]
  R4 = Resistor [tolerance=±5% power=0.25W resistance=220 package=THT]
  Q2 = NPN-Transistor [package="TO92 [THT]"]
  C1 = Ceramic Capacitor [capacitance=100nF voltage=35V package="100 mil [THT, multilayer]"]
  C2 = Ceramic Capacitor [capacitance=100nF voltage=35V package="100 mil [THT, multilayer]"]
  R5 = Resistor [tolerance=±5% power=0.25W resistance=220 package=THT]
  R6 = Resistor [tolerance=±5% power=0.25W resistance=220 package=THT]
  MIC1 = Microphone
  C3 = Ceramic Capacitor [capacitance=100nF voltage=35V package="100 mil [THT, multilayer]"]
  R7 = Resistor [tolerance=±5% power=0.25W resistance=220 package=THT]
  R8 = Resistor [tolerance=±5% power=0.25W resistance=220 package=THT]

nets:
  N1: J1.pin1, C1.1
  N2: J1.pin2, R2.Pin_0, R4.Pin_0, R6.Pin_0, MIC1.pin1, R8.Pin_0
  N3: VCC1.+, R1.Pin_1, R3.Pin_1, R5.Pin_1, R7.Pin_1
  N4: R1.Pin_0, Q1.E, C3.0
  N5: Q1.B, C2.1, R5.Pin_0, R6.Pin_1
  N6: R3.Pin_0, Q2.E, C1.0
  N7: R4.Pin_1, Q2.C
  N8: Q2.B, C3.1, R7.Pin_0, R8.Pin_1
  N9: C2.0, MIC1.pin2
