# Fritzing sketch CMOS_NOR_Gate (saved by Fritzing 1.0.3b)
breadboards: 1

parts:
  VCC1 = Battery [internal_resistance=0.1Ω]
  S1 = Momentary Switch [package=ksa_sealed_tac_switch]
  S2 = Momentary Switch [package=ksa_sealed_tac_switch]
  Q1 = Basic FET P-Channel [package="DPak [SMD]"]
  Q2 = Basic FET P-Channel [package="TO220 [THT]"]
  Q3 = Basic FET N-Channel [package="TO220 [THT]"]
  Q4 = Basic FET N-Channel [package="TO220 [THT]"]
  R1 = Resistor [tolerance=±5% power=0.25W resistance=220 package=THT]
  LED1 = LED - 5mm [color="Red (633nm)" current=0.030A package="5 mm [THT]"]

nets:
  N1: VCC1.-, Q3.source, Q4.source, LED1.anode
  N2: VCC1.+, S1.1, S1.3, S2.1, S2.3, Q1.drain
  N3: S1.4, Q1.Gate, Q3.gate
  N4: S2.4, Q2.gate, Q4.gate
  N5: Q1.source, Q2.source, Q3.drain, Q4.drain, R1.Pin_0
  N6: R1.Pin_1, LED1.cathode
