// Logisim project SR_Latch.circ as structural Verilog: 1 circuit, main circuit main
module main (
);

  wire button_1_out, button_2_out, nand_1_out, nand_2_out;

  Button button_1 (.out(button_1_out));
  Button button_2 (.out(button_2_out));
  nand nand_1 (nand_1_out, button_1_out, nand_2_out);
  nand nand_2 (nand_2_out, nand_1_out, button_2_out);
  LED led_1 (.in(nand_1_out));
  LED led_2 (.in(nand_2_out));
endmodule
